// Digital circuit q-clock-v2.dig as structural Verilog
module q_clock_v2 (
  input  Scan,
  input  Clock,
  input  BRK,
  input  Manual,
  input  Auto,
  output Inverted,
  output Primary
);

  wire and_1_out, and_2_out, and_3_out, and_4_out, d_ff_1_q, d_ff_2_q, d_ff_3_nq, d_ff_3_q, d_ff_4_nq,
       d_ff_4_q, nor_1_out, nor_2_out, or_1_out, or_2_out, xor_1_out, xor_2_out;

  LED led_1 (.in(d_ff_3_q));
  PullDown pulldown_1 (.out(Auto));
  LED led_2 (.in(d_ff_3_nq));
  PullDown pulldown_2 (.out(Manual));
  xor xor_1 (xor_1_out, Clock, 1'b1);
  D_FF d_ff_1 (.D(Manual), .C(Scan), .Q(d_ff_1_q));  // open: nQ
  or or_1 (or_1_out, Auto, nor_1_out);
  nor nor_1 (nor_1_out, or_2_out, d_ff_3_nq);
  D_FF d_ff_2 (.D(d_ff_1_q), .C(Scan), .Q(d_ff_2_q));  // open: nQ
  D_FF d_ff_3 (.D(or_1_out), .C(xor_1_out), .Q(d_ff_3_q), .nQ(d_ff_3_nq));
  xor xor_2 (xor_2_out, d_ff_1_q, d_ff_2_q);
  and and_1 (and_1_out, Clock, d_ff_3_q);
  and and_2 (and_2_out, d_ff_3_nq, xor_2_out);
  and and_3 (and_3_out, d_ff_4_q, d_ff_2_q);
  and and_4 (and_4_out, BRK, d_ff_4_nq);
  nor nor_2 (nor_2_out, and_1_out, and_2_out);
  or or_2 (or_2_out, and_3_out, and_4_out);
  D_FF d_ff_4 (.D(d_ff_4_nq), .C(nor_2_out), .Q(d_ff_4_q), .nQ(d_ff_4_nq));
  nor nor_3 (Inverted, nor_2_out, d_ff_4_q);
  nor nor_4 (Primary, d_ff_4_nq, nor_2_out);

  // Notes on the sheet:
  //   Scan: Hz: 2
  //   Mode switch
  //   Debounce/pulse
  //   Clock source sel.
  //   Man. phase sel.
  //   Divider
endmodule
